// Logisim project logism_design.circ as structural Verilog: 8 circuits, main circuit processor
module processor (
  input  [17:0] ASSEMBLY_INPUT
);

  ALU alu_1 (.OP(ASSEMBLY_INPUT[2:0]), .IMM(ASSEMBLY_INPUT[17:12]));  // open: REGINPUT1, REGINPUT2, out_5

  // Other names for the same wires on the sheet: ADDR[9:0] = ASSEMBLY_INPUT[13:4]; REG0[3:0] = ASSEMBLY_INPUT[7:4];
  //   REG1[3:0] = ASSEMBLY_INPUT[11:8]; IMM[5:0] = ASSEMBLY_INPUT[17:12]; REG2[3:0] = ASSEMBLY_INPUT[15:12];
  //   OPCODE[3:0] = ASSEMBLY_INPUT[3:0]

  // Notes on the sheet:
  //   OP CODE
endmodule

module half_adder (
  input  A,
  input  B,
  output out_3,
  output out_4
);

  xor xor_1 (out_3, A, B);
  and and_1 (out_4, A, B);
endmodule

module full_adder (
  input  in_1,
  input  in_2,
  input  in_3,
  output out_4,
  output out_5
);

  wire and_1_out, and_2_out, xor_1_out;

  xor xor_1 (xor_1_out, in_1, in_2);
  xor xor_2 (out_4, xor_1_out, in_3);
  and and_1 (and_1_out, xor_1_out, in_3);
  and and_2 (and_2_out, in_2, in_1);
  or or_1 (out_5, and_1_out, and_2_out);
endmodule

module ALU (
  input  [17:0] REGINPUT1,
  input  [17:0] REGINPUT2,
  input  [5:0] IMM,
  input  [2:0] OP,
  output [17:0] out_5
);

  wire [17:0] ADD18_a_2, ADDIMM_a_2, AND18_a_2, ANDIMM_a_2, NAND18_a_2, NOR18_a_2;

  _18_bit_adder ADD18 (.A(REGINPUT2), .B(REGINPUT1), .A_2(ADD18_a_2));
  _18_bit_and AND18 (.A(REGINPUT2), .B(REGINPUT1), .A_2(AND18_a_2));
  Multiplexer #(.select(3), .width(18), .enable("false")) multiplexer_1 (
    .in0(ADD18_a_2), .in1(ADDIMM_a_2), .in2(AND18_a_2), .in3(ANDIMM_a_2), .in4(NOR18_a_2), .in5(NAND18_a_2),
    .out(out_5), .sel(OP));  // open: in6, in7
  _18_bit_nand NAND18 (.A(REGINPUT2), .B(REGINPUT1), .A_2(NAND18_a_2));
  _18_bit_nor NOR18 (.A(REGINPUT2), .B(REGINPUT1), .A_2(NOR18_a_2));
  _18_bit_adder ADDIMM (.A({{12{1'b0}}, IMM}), .B(REGINPUT1), .A_2(ADDIMM_a_2));
  _18_bit_and ANDIMM (.A({{12{1'b0}}, IMM}), .B(REGINPUT1), .A_2(ANDIMM_a_2));

  // Notes on the sheet:
  //   BIT EXTENSION
endmodule

module _18_bit_adder (
  input  [17:0] A,
  input  [17:0] B,
  output [17:0] A_2
);

  wire full_adder_1_out_5, full_adder_2_out_5, full_adder_3_out_5, full_adder_4_out_5, full_adder_5_out_5,
       full_adder_6_out_5, full_adder_7_out_5, full_adder_8_out_5, full_adder_9_out_5, full_adder_10_out_5,
       full_adder_11_out_5, full_adder_12_out_5, full_adder_13_out_5, full_adder_14_out_5,
       full_adder_15_out_5, full_adder_16_out_5, full_adder_17_out_5;

  full_adder full_adder_1 (.in_1(1'b0), .in_2(B[0]), .in_3(A[0]), .out_4(A_2[0]), .out_5(full_adder_1_out_5));
  full_adder full_adder_2 (
    .in_1(full_adder_1_out_5), .in_2(B[1]), .in_3(A[1]), .out_4(A_2[1]), .out_5(full_adder_2_out_5));
  full_adder full_adder_3 (
    .in_1(full_adder_2_out_5), .in_2(B[2]), .in_3(A[2]), .out_4(A_2[2]), .out_5(full_adder_3_out_5));
  full_adder full_adder_4 (
    .in_1(full_adder_3_out_5), .in_2(B[3]), .in_3(A[3]), .out_4(A_2[3]), .out_5(full_adder_4_out_5));
  full_adder full_adder_5 (
    .in_1(full_adder_4_out_5), .in_2(B[4]), .in_3(A[4]), .out_4(A_2[4]), .out_5(full_adder_5_out_5));
  full_adder full_adder_6 (
    .in_1(full_adder_5_out_5), .in_2(B[5]), .in_3(A[5]), .out_4(A_2[5]), .out_5(full_adder_6_out_5));
  full_adder full_adder_7 (
    .in_1(full_adder_6_out_5), .in_2(B[6]), .in_3(A[6]), .out_4(A_2[6]), .out_5(full_adder_7_out_5));
  full_adder full_adder_8 (
    .in_1(full_adder_7_out_5), .in_2(B[7]), .in_3(A[7]), .out_4(A_2[7]), .out_5(full_adder_8_out_5));
  full_adder full_adder_9 (
    .in_1(full_adder_8_out_5), .in_2(B[8]), .in_3(A[8]), .out_4(A_2[8]), .out_5(full_adder_9_out_5));
  full_adder full_adder_10 (
    .in_1(full_adder_9_out_5), .in_2(B[9]), .in_3(A[9]), .out_4(A_2[9]), .out_5(full_adder_10_out_5));
  full_adder full_adder_11 (
    .in_1(full_adder_10_out_5), .in_2(B[10]), .in_3(A[10]), .out_4(A_2[10]), .out_5(full_adder_11_out_5));
  full_adder full_adder_12 (
    .in_1(full_adder_11_out_5), .in_2(A[11]), .in_3(B[11]), .out_4(A_2[11]), .out_5(full_adder_12_out_5));
  full_adder full_adder_13 (
    .in_1(full_adder_12_out_5), .in_2(A[12]), .in_3(B[12]), .out_4(A_2[12]), .out_5(full_adder_13_out_5));
  full_adder full_adder_14 (
    .in_1(full_adder_13_out_5), .in_2(A[13]), .in_3(B[13]), .out_4(A_2[13]), .out_5(full_adder_14_out_5));
  full_adder full_adder_15 (
    .in_1(full_adder_14_out_5), .in_2(A[14]), .in_3(B[14]), .out_4(A_2[14]), .out_5(full_adder_15_out_5));
  full_adder full_adder_16 (
    .in_1(full_adder_15_out_5), .in_2(B[15]), .in_3(A[15]), .out_4(A_2[15]), .out_5(full_adder_16_out_5));
  full_adder full_adder_17 (
    .in_1(full_adder_16_out_5), .in_2(B[16]), .in_3(A[16]), .out_4(A_2[16]), .out_5(full_adder_17_out_5));
  full_adder full_adder_18 (.in_1(full_adder_17_out_5), .in_2(A[17]), .in_3(B[17]), .out_4(A_2[17]));  // open: out_5
endmodule

module _18_bit_and (
  input  [17:0] A,
  input  [17:0] B,
  output [17:0] A_2
);

  and and_1 (A_2[0], A[0], B[0]);
  and and_2 (A_2[1], A[1], B[1]);
  and and_3 (A_2[2], A[2], B[2]);
  and and_4 (A_2[3], A[3], B[3]);
  and and_5 (A_2[4], A[4], B[4]);
  and and_6 (A_2[5], A[5], B[5]);
  and and_7 (A_2[6], A[6], B[6]);
  and and_8 (A_2[7], A[7], B[7]);
  and and_9 (A_2[8], A[8], B[8]);
  and and_10 (A_2[9], A[9], B[9]);
  and and_11 (A_2[10], A[10], B[10]);
  and and_12 (A_2[11], A[11], B[11]);
  and and_13 (A_2[12], A[12], B[12]);
  and and_14 (A_2[13], A[13], B[13]);
  and and_15 (A_2[14], A[14], B[14]);
  and and_16 (A_2[15], A[15], B[15]);
  and and_17 (A_2[16], A[16], B[16]);
  and and_18 (A_2[17], A[17], B[17]);
endmodule

module _18_bit_nand (
  input  [17:0] A,
  input  [17:0] B,
  output [17:0] A_2
);

  nand nand_1 (A_2[0], A[0], B[0]);
  nand nand_2 (A_2[1], A[1], B[1]);
  nand nand_3 (A_2[2], A[2], B[2]);
  nand nand_4 (A_2[3], A[3], B[3]);
  nand nand_5 (A_2[4], A[4], B[4]);
  nand nand_6 (A_2[5], A[5], B[5]);
  nand nand_7 (A_2[6], A[6], B[6]);
  nand nand_8 (A_2[7], A[7], B[7]);
  nand nand_9 (A_2[8], A[8], B[8]);
  nand nand_10 (A_2[9], A[9], B[9]);
  nand nand_11 (A_2[10], A[10], B[10]);
  nand nand_12 (A_2[11], A[11], B[11]);
  nand nand_13 (A_2[12], A[12], B[12]);
  nand nand_14 (A_2[13], A[13], B[13]);
  nand nand_15 (A_2[14], A[14], B[14]);
  nand nand_16 (A_2[15], A[15], B[15]);
  nand nand_17 (A_2[16], A[16], B[16]);
  nand nand_18 (A_2[17], A[17], B[17]);
endmodule

module _18_bit_nor (
  input  [17:0] A,
  input  [17:0] B,
  output [17:0] A_2
);

  nor nor_1 (A_2[0], A[0], B[0]);
  nor nor_2 (A_2[1], A[1], B[1]);
  nor nor_3 (A_2[2], A[2], B[2]);
  nor nor_4 (A_2[3], A[3], B[3]);
  nor nor_5 (A_2[4], A[4], B[4]);
  nor nor_6 (A_2[5], A[5], B[5]);
  nor nor_7 (A_2[6], A[6], B[6]);
  nor nor_8 (A_2[7], A[7], B[7]);
  nor nor_9 (A_2[8], A[8], B[8]);
  nor nor_10 (A_2[9], A[9], B[9]);
  nor nor_11 (A_2[10], A[10], B[10]);
  nor nor_12 (A_2[11], A[11], B[11]);
  nor nor_13 (A_2[12], A[12], B[12]);
  nor nor_14 (A_2[13], A[13], B[13]);
  nor nor_15 (A_2[14], A[14], B[14]);
  nor nor_16 (A_2[15], A[15], B[15]);
  nor nor_17 (A_2[16], A[16], B[16]);
  nor nor_18 (A_2[17], A[17], B[17]);
endmodule
